# Fritzing sketch stewart2 (saved by Fritzing 0.9.9b)
circuit board: 14.5196cm x 11.4252cm

parts:
  LCD_1602 = LCD Display 16x2 [part_number=LCD]
  LED2 = LED - 5mm [color="Red (633nm)" current=0.030 package="5 mm [THT]"]
  LED3 = LED - 5mm [color="Red (633nm)" current=0.030 package="5 mm [THT]"]
  LED4 = LED - 5mm [color="Red (633nm)" current=0.030 package="5 mm [THT]"]
  R1 = Resistor [tolerance=±5% resistance=220 package="0805 [SMD]"]
  R3 = Resistor [tolerance=±5% resistance=220 package="0805 [SMD]"]
  R4 = Resistor [tolerance=±5% resistance=220 package="0805 [SMD]"]
  SERVO_1 = Header 4 [package=jst-4-pth]
  SERVO_0 = Header 4 [package=jst-4-pth]
  SERVO_5 = Header 4 [package=jst-4-pth]
  SERVO_4 = Header 4 [package=jst-4-pth]
  SERVO_2 = Header 4 [package=jst-4-pth]
  XYZ = Header 5 [package=jst-5-pth]
  RPY = Header 5 [package=jst-5-pth]
  ARDUINO_DUE = Arduino Due (Rev2b)
  6_8v = Power Jack [package=power_jack_slot]
  SERVO_3 = Header 4 [package=jst-4-pth]
  Switches = Header 4 [package=jst-4-pth]

nets:
  N1: LCD_1602.aún_sin_nombre#0, LCD_1602.aún_sin_nombre#4
  N2: LCD_1602.aún_sin_nombre#3, ARDUINO_DUE.D14/TX3
  N3: LCD_1602.aún_sin_nombre#5, ARDUINO_DUE.D15/RX3
  N4: LCD_1602.aún_sin_nombre#10, ARDUINO_DUE.D16/TX2
  N5: LCD_1602.aún_sin_nombre#11, ARDUINO_DUE.D17/RX2
  N6: LCD_1602.aún_sin_nombre#12, ARDUINO_DUE.D18/TX1
  N7: LCD_1602.aún_sin_nombre#13, ARDUINO_DUE.D19/RX1
  N8: LED2.cathode, R4.Pin_1
  N9: LED2.anode, ARDUINO_DUE.D3_PWM
  N10: LED3.cathode, R1.Pin_1
  N11: LED3.anode, ARDUINO_DUE.D4_PWM/SS1
  N12: LED4.cathode, R3.Pin_1
  N13: LED4.anode, ARDUINO_DUE.D5_PWM
  GND: R1.Pin_0, R3.Pin_0, R4.Pin_0, SERVO_1.1, SERVO_0.1, SERVO_5.1, SERVO_4.1, SERVO_2.1, XYZ.4, RPY.4, ARDUINO_DUE.GND, 6_8v.GND, SERVO_3.1, Switches.1
  N14: SERVO_1.2, SERVO_0.2, SERVO_5.2, SERVO_4.2, SERVO_2.2, 6_8v.PWR, SERVO_3.2
  N15: SERVO_1.4, ARDUINO_DUE.D10_PWM/SS0
  N16: SERVO_0.4, ARDUINO_DUE.D11_PWM
  N17: SERVO_5.4, ARDUINO_DUE.D6_PWM
  N18: SERVO_4.4, ARDUINO_DUE.D7_PWM
  N19: SERVO_2.4, ARDUINO_DUE.D9_PWM
  N20: XYZ.1, ARDUINO_DUE.A2
  N21: XYZ.2, ARDUINO_DUE.A1
  N22: XYZ.3, ARDUINO_DUE.A0
  N23: XYZ.5, RPY.5, ARDUINO_DUE.IOREF
  N24: RPY.1, ARDUINO_DUE.A5
  N25: RPY.2, ARDUINO_DUE.A4
  N26: RPY.3, ARDUINO_DUE.A3
  N27: ARDUINO_DUE.D8_PWM, SERVO_3.4
  N28: ARDUINO_DUE.D44, Switches.3
  N29: ARDUINO_DUE.D45, Switches.4
  N30: ARDUINO_DUE.D46, Switches.2

notes:
  Time
  Position
  Jitter

custom parts:
  Header 5: Header 5 Standard 5-pin 2mm header. Rev3
